# Fritzing sketch display_weather_information (saved by Fritzing 0.9.4)
breadboards: 1

parts:
  Mod1 = Raspberry Pi Pico
  LCD1 = LCD screen  # not connected
  パーツ1 = BME280

nets:
  N1: Mod1.pin_3, Mod1.pin_8, Mod1.pin_13, Mod1.pin_18, Mod1.pin_23, Mod1.pin_28, Mod1.pin_33, Mod1.pin_38, パーツ1.GND
  N2: Mod1.pin_16, パーツ1.SDA
  N3: Mod1.pin_17, パーツ1.SCL
  N4: Mod1.pin_36, パーツ1.VIN

notes:
  ディスプレイ
  温湿度・気圧センサ
  GND
  3V3
  Vbus
  12
  13
  SCL
  SDA
  VCC
  SDO

custom parts:
  Raspberry Pi Pico: Raspberry Pi Pico. Based around the RP2040 microcontroller the Pico is a low cost microcontroller device bringing Raspberry Pi quality, cost, and easy of use to the microcontroller space. Jan 2021, Split part in to two versions: tht (this one) and SMD. This one will drill holes for a .1 in header in pcb to allow plugging in the module as well as providing pads to solder the module to the top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
